# Fritzing sketch Kincony KC868-A6 DMX (saved by Fritzing 1.0.3b)

parts:
  J2 = Camdenboss CTB0158-2 [part_number=CTB0158-2 package=THT]
  J1 = Camdenboss CTB0158-7 [part_number=CTB0158-7 package=THT]
  J3 = Camdenboss CTB0158-7 [part_number=CTB0158-7 package=THT]  # not connected
  J4 = Camdenboss CTB0158-5 [part_number=CTB0158-5 package=THT]  # not connected
  J5 = Camdenboss CTB0158-3 [part_number=CTB0158-3 package=THT]

nets:
  N1: J2.terminal_1, J5.terminal_1
  N2: J2.terminal_2, J5.terminal_2
  N3: J1.terminal_1, J5.terminal_3

notes:
  D+
  D-
  GND
