# Fritzing sketch Kincony KC868-A6 (saved by Fritzing 1.0.3b)

parts:
  J1 = Camdenboss CTB0158-5 [part_number=CTB0158-5 package=THT]  # not connected
  J3 = Camdenboss CTB0158-7 [part_number=CTB0158-7 package=THT]  # not connected
  J4 = Camdenboss CTB0158-7 [part_number=CTB0158-7 package=THT]
  J5 = Camdenboss CTB0158-2 [part_number=CTB0158-2 package=THT]
  X1 = DB9 Connector [package=db9]  # not connected
  J2 = double row female pin header, 4 pins [form="♀ (female)"]  # not connected
  J7 = double row female pin header, 4 pins [form="♀ (female)"]  # not connected
  J6 = Camdenboss CTB0158-2 [part_number=CTB0158-2 package=THT]  # not connected
  NEOPIXEL1 = Neopixel Strip -- White (30/m)
  A1 = DY-HV20T
  J8 = double row female pin header, 4 pins [form="♀ (female)"]
  JACK1 = 2.1mm Barrel Jack with Terminal Block  # not connected
  BULB1 = Incandescent light bulb small [package="bulb sm"]  # not connected
  J9 = female pin header, 4 pins [form="♀ (female)"]

nets:
  N1: J4.terminal_4, NEOPIXEL1.GND
  N2: J4.terminal_6, NEOPIXEL1.Din
  N3: J5.terminal_1, J9.pin2
  N4: J5.terminal_2, J9.pin1
  N5: A1.Pin_5, J8.pin3
  N6: A1.Pin_6, J8.pin4
  N7: A1.Pin_14, J8.pin1

notes:
  MG128-5.00 Terminal Blocks
  NO    C    NC
  Relay 1
  Relay 2
  Relay 3
  Relay 4
  Relay 5
  Relay 6
  JM2EDG-5.0 Terminal Block
  15EDGK-3.81 Terminal Blocks
  For reasons I don't understand do NOT connect the - INPUT line from the Controller, or else
  the V1-T resets immediately.
  White +/A
  Green -/B
  GND
  12V

custom parts:
  Neopixel Strip -- White (30/m): These NeoPixel strips have 30 digitally-addressable pixel LEDs per meter and are very affordable and are only 12.5 mm wide, 10 mm if you remove the strip from the casing.
  DY-HV20T: DY-HV20T 12V/24V Power supply10W/20W Voice Playback Module Supporting Micro SD Card MP3 Music Player for Arduino.
